# Fritzing sketch Nano_ESP32-PCB_HC12-1 (saved by Fritzing 1.0.5)
circuit board: 4.02871cm x 14.3441cm

parts:
  Arduino_Nano_ESP32 = Arduino Nano (Rev3.0)
  HC-12_module = female pin header, 5 pins [form="♀ (female)"]
  Nano_ESP32 = Arduino Nano v2.3
  HC-12_module1 = female pin header, 5 pins [form="♀ (female)"]
  Part3 = Arduino Nano (Rev3.0)

nets:
  N1: Arduino_Nano_ESP32.D1/TX, Nano_ESP32.D1TX
  N2: Arduino_Nano_ESP32.D0/RX, Nano_ESP32.D0RX
  N3: Arduino_Nano_ESP32.RESET, Nano_ESP32.RST
  GND: Arduino_Nano_ESP32.GND, HC-12_module.pin2, Nano_ESP32.GND
  N4: Arduino_Nano_ESP32.D2, Nano_ESP32.D2
  N5: Arduino_Nano_ESP32.D3, Nano_ESP32.D3
  N6: Arduino_Nano_ESP32.D4, HC-12_module.pin3, Nano_ESP32.D4
  N7: Arduino_Nano_ESP32.D5, Nano_ESP32.D5
  N8: Arduino_Nano_ESP32.D6, Nano_ESP32.D6
  N9: Arduino_Nano_ESP32.D7, Nano_ESP32.D7
  N10: Arduino_Nano_ESP32.D8, Nano_ESP32.D8
  N11: Arduino_Nano_ESP32.D9, Nano_ESP32.D9
  N12: Arduino_Nano_ESP32.D10, Nano_ESP32.D10
  N13: Arduino_Nano_ESP32.D11/MOSI, Nano_ESP32.D11
  N14: Arduino_Nano_ESP32.D12/MISO, Nano_ESP32.D12
  VIN: Arduino_Nano_ESP32.VIN, Nano_ESP32.VIN
  N15: Arduino_Nano_ESP32.5V, HC-12_module.pin1
  N16: Arduino_Nano_ESP32.A7, Nano_ESP32.A0
  N17: Arduino_Nano_ESP32.A6, Nano_ESP32.A1
  N18: Arduino_Nano_ESP32.A5, Nano_ESP32.A2
  N19: Arduino_Nano_ESP32.A4, Nano_ESP32.A3
  N20: Arduino_Nano_ESP32.A3, Nano_ESP32.A4
  N21: Arduino_Nano_ESP32.A2, Nano_ESP32.A5
  N22: Arduino_Nano_ESP32.A1, Nano_ESP32.A6
  N23: Arduino_Nano_ESP32.A0, Nano_ESP32.A7
  N24: Arduino_Nano_ESP32.AREF, Nano_ESP32.AREF
  3V3: Arduino_Nano_ESP32.3V3, Nano_ESP32.3V3
  N25: Arduino_Nano_ESP32.D13/SCK, Nano_ESP32.D13
  N26: HC-12_module1.pin1, Part3.5V
  N27: HC-12_module1.pin2, Part3.GND
  N28: HC-12_module1.pin4, Part3.D0/RX

notes:
  Gnd
  TXD
  RXD
  VCC
  5V
  A5
  A4
  D5
  A3
  A2
  TX
  RX
  D6
  D8
  D9
  D10
  D11
  D12
  A1
  A6
  A7
  Vin
  B1
  Rst
  D4
  D3
  D2
  A0
  Aref
  3V3
  D13
  USB
  D7
  Ed Nieuwenhuys 2026
  USB side
  SET
